// Digital circuit ADDER.dig as structural Verilog
module ADDER (
  input  A,
  input  B,
  input  C,
  input  [1:0] A_2,
  input  B_2,
  input  C_2,
  input  D,
  input  E,
  input  F,
  input  G,
  input  H,
  input  [7:0] _8BIT_INPUT__BUS,
  output OUTPUT_B,
  output OUTPUT_A
);

  wire halfadder_1_p6, halfadder_1_p7, halfadder_2_p3;

  // HALFADDER halfadder_1: pin names not known; wires that end beside it: A_2, B_2, C_2, A, B, halfadder_1_p6, halfadder_1_p7
  // HALFADDER halfadder_2: pin names not known; wires that end beside it: C, halfadder_1_p7, halfadder_2_p3, OUTPUT_B
  ORGate orgate_1 (.A(halfadder_1_p6), .B(halfadder_2_p3), .OUTPUT(OUTPUT_A));

  // Notes on the sheet:
  //   8 BIT MAX NUMER=255
endmodule
