// Digital circuit ADDER16BIT.dig as structural Verilog
module ADDER16BIT (
  input  A1,
  input  A2,
  input  A3,
  input  A4,
  input  A5,
  input  A6,
  input  A7,
  input  A8,
  input  A9,
  input  A10,
  input  A11,
  input  A12,
  input  A13,
  input  A14,
  input  A15,
  input  A16,
  input  B1,
  input  B2,
  input  B3,
  input  B4,
  input  B5,
  input  B6,
  input  B7,
  input  B8,
  input  B9,
  input  B10,
  input  B11,
  input  B12,
  input  B13,
  input  B14,
  input  B15,
  input  B16,
  input  C4,
  output A,
  output B,
  output C,
  output D,
  output E,
  output F,
  output G,
  output H,
  output I,
  output J,
  output K,
  output L,
  output M,
  output N,
  output O,
  output P,
  output Q
);

  wire adder8bit_1_a;

  ADDER8BIT adder8bit_1 (
    .A1(A9), .A2(A10), .A3(A11), .A4(A12), .A5(A13), .A6(A14), .A7(A15), .A8(A16), .B1(B9), .B2(B10),
    .B3(B11), .B4(B12), .B5(B13), .B6(B14), .B7(B15), .B8(B16), .C3(C4), .A(adder8bit_1_a), .B(J), .C(K),
    .D(L), .E(M), .F(N), .G(O), .H(P), .I(Q));
  ADDER8BIT adder8bit_2 (
    .A1(A1), .A2(A2), .A3(A3), .A4(A4), .A5(A5), .A6(A6), .A7(A7), .A8(A8), .B1(B1), .B2(B2), .B3(B3),
    .B4(B4), .B5(B5), .B6(B6), .B7(B7), .B8(B8), .C3(adder8bit_1_a), .A(A), .B(B), .C(C), .D(D), .E(E),
    .F(F), .G(G), .H(H), .I(I));
endmodule
