// Digital circuit ADDER1bit.dig as structural Verilog
module ADDER1bit (
  input  INPUT_CARRY_A,
  input  B,
  input  C,
  output OUTPUT_B,
  output CARRY_A
);

  wire halfadder_1_p3, halfadder_1_p4, halfadder_2_p4;

  // HALFADDER halfadder_1: pin names not known; wires that end beside it: INPUT_CARRY_A, B, halfadder_1_p3, halfadder_1_p4
  // HALFADDER halfadder_2: pin names not known; wires that end beside it: halfadder_1_p3, C, OUTPUT_B, halfadder_2_p4
  ORGate orgate_1 (.A(halfadder_1_p4), .B(halfadder_2_p4), .OUTPUT(CARRY_A));
endmodule
