// Digital circuit ADDER2bit.dig as structural Verilog
module ADDER2bit (
  input  A1,
  input  A2,
  input  B1,
  input  B2,
  input  C1,
  output A,
  output B,
  output C
);

  wire adder1bit_1_carry_a;

  ADDER1bit adder1bit_1 (.INPUT_CARRY_A(A2), .B(B2), .C(C1), .OUTPUT_B(C), .CARRY_A(adder1bit_1_carry_a));
  ADDER1bit adder1bit_2 (.INPUT_CARRY_A(A1), .B(B1), .C(adder1bit_1_carry_a), .OUTPUT_B(B), .CARRY_A(A));
endmodule
