// Digital circuit ADDER32BIT.dig as structural Verilog
module ADDER32BIT (
  input  A1,
  input  A2,
  input  A3,
  input  A4,
  input  A5,
  input  A6,
  input  A7,
  input  A8,
  input  A9,
  input  A10,
  input  A11,
  input  A12,
  input  A13,
  input  A14,
  input  A15,
  input  A16,
  input  A17,
  input  A18,
  input  A19,
  input  A20,
  input  A21,
  input  A22,
  input  A23,
  input  A24,
  input  A25,
  input  A26,
  input  A27,
  input  A28,
  input  A29,
  input  A30,
  input  A31,
  input  A32,
  input  B1,
  input  B2,
  input  B3,
  input  B4,
  input  B5,
  input  B6,
  input  B7,
  input  B8,
  input  B9,
  input  B10,
  input  B11,
  input  B12,
  input  B13,
  input  B14,
  input  B15,
  input  B16,
  input  B17,
  input  B18,
  input  B19,
  input  B20,
  input  B21,
  input  B22,
  input  B23,
  input  B24,
  input  B25,
  input  B26,
  input  B27,
  input  B28,
  input  B29,
  input  B30,
  input  B31,
  input  B32,
  input  C5,
  output D1,
  output D2,
  output D3,
  output D4,
  output D5,
  output D6,
  output D7,
  output D8,
  output D9,
  output D10,
  output D11,
  output D12,
  output D13,
  output D14,
  output D15,
  output D16,
  output D17,
  output D18,
  output D19,
  output D20,
  output D21,
  output D22,
  output D23,
  output D24,
  output D25,
  output D26,
  output D27,
  output D28,
  output D29,
  output D30,
  output D31,
  output D32,
  output D33
);

  wire adder16bit_1_a;

  ADDER16BIT adder16bit_1 (
    .A1(A17), .A2(A18), .A3(A19), .A4(A20), .A5(A21), .A6(A22), .A7(A23), .A8(A24), .A9(A25), .A10(A26),
    .A11(A27), .A12(A28), .A13(A29), .A14(A30), .A15(A31), .A16(A32), .B1(B17), .B2(B18), .B3(B19), .B4(B20),
    .B5(B21), .B6(B22), .B7(B23), .B8(B24), .B9(B25), .B10(B26), .B11(B27), .B12(B28), .B13(B29), .B14(B30),
    .B15(B31), .B16(B32), .C4(C5), .A(adder16bit_1_a), .B(D18), .C(D19), .D(D20), .E(D21), .F(D22), .G(D23),
    .H(D24), .I(D25), .J(D26), .K(D27), .L(D28), .M(D29), .N(D30), .O(D31), .P(D32), .Q(D33));
  ADDER16BIT adder16bit_2 (
    .A1(A1), .A2(A2), .A3(A3), .A4(A4), .A5(A5), .A6(A6), .A7(A7), .A8(A8), .A9(A9), .A10(A10), .A11(A11),
    .A12(A12), .A13(A13), .A14(A14), .A15(A15), .A16(A16), .B1(B1), .B2(B2), .B3(B3), .B4(B4), .B5(B5),
    .B6(B6), .B7(B7), .B8(B8), .B9(B9), .B10(B10), .B11(B11), .B12(B12), .B13(B13), .B14(B14), .B15(B15),
    .B16(B16), .C4(adder16bit_1_a), .A(D1), .B(D2), .C(D3), .D(D4), .E(D5), .F(D6), .G(D7), .H(D8), .I(D9),
    .J(D10), .K(D11), .L(D12), .M(D13), .N(D14), .O(D15), .P(D16), .Q(D17));
endmodule
