// Digital circuit ADDER3BIT.dig as structural Verilog
module ADDER3BIT (
  input  A1,
  input  A2,
  input  A3,
  input  B1,
  input  B2,
  input  B3,
  output B,
  output C,
  output D,
  output A
);

  wire adder2bit_1_carry_a;

  ADDER2bit adder2bit_1 (.A1(A2), .A2(A3), .B1(B2), .B2(B3), .OUTPUT_C(D), .OUTPUT_B(C), .CARRY_A(adder2bit_1_carry_a));
  ADDER1bit adder1bit_1 (.INPUT_CARRY_A(adder2bit_1_carry_a), .B(A1), .C(B1), .OUTPUT_B(B), .CARRY_A(A));
endmodule
