// Digital circuit ADDER4bit.dig as structural Verilog
module ADDER4bit (
  input  A1,
  input  A2,
  input  A3,
  input  A4,
  input  B1,
  input  B2,
  input  B3,
  input  B4,
  output A,
  output B,
  output C,
  output D,
  output E
);

  wire adder3bit_1_a;

  ADDER3BIT adder3bit_1 (.A1(A2), .A2(A3), .A3(A4), .B1(B2), .B2(B3), .B3(B4), .B(C), .C(D), .D(E), .A(adder3bit_1_a));
  ADDER1bit adder1bit_1 (.INPUT_CARRY_A(adder3bit_1_a), .B(A1), .C(B1), .OUTPUT_B(B), .CARRY_A(A));
endmodule
