// Digital circuit ADDER64BIT.dig as structural Verilog
module ADDER64BIT (
  input  A1,
  input  A2,
  input  A3,
  input  A4,
  input  A5,
  input  A6,
  input  A7,
  input  A8,
  input  A9,
  input  A10,
  input  A11,
  input  A12,
  input  A13,
  input  A14,
  input  A15,
  input  A16,
  input  A17,
  input  A18,
  input  A19,
  input  A20,
  input  A21,
  input  A22,
  input  A23,
  input  A24,
  input  A25,
  input  A26,
  input  A27,
  input  A28,
  input  A29,
  input  A30,
  input  A31,
  input  A32,
  input  A33,
  input  A34,
  input  A35,
  input  A36,
  input  A37,
  input  A38,
  input  A39,
  input  A40,
  input  A41,
  input  A42,
  input  A43,
  input  A44,
  input  A45,
  input  A46,
  input  A47,
  input  A48,
  input  A49,
  input  A50,
  input  A51,
  input  A52,
  input  A53,
  input  A54,
  input  A55,
  input  A56,
  input  A57,
  input  A58,
  input  A59,
  input  A60,
  input  A61,
  input  A62,
  input  A63,
  input  A64,
  input  B1,
  input  B2,
  input  B3,
  input  B4,
  input  B5,
  input  B6,
  input  B7,
  input  B8,
  input  B9,
  input  B10,
  input  B11,
  input  B12,
  input  B13,
  input  B14,
  input  B15,
  input  B16,
  input  B17,
  input  B18,
  input  B19,
  input  B20,
  input  B21,
  input  B22,
  input  B23,
  input  B24,
  input  B25,
  input  B26,
  input  B27,
  input  B28,
  input  B29,
  input  B30,
  input  B31,
  input  B32,
  input  B33,
  input  B34,
  input  B35,
  input  B36,
  input  B37,
  input  B38,
  input  B39,
  input  B40,
  input  B41,
  input  B42,
  input  B43,
  input  B44,
  input  B45,
  input  B46,
  input  B47,
  input  B48,
  input  B49,
  input  B50,
  input  B51,
  input  B52,
  input  B53,
  input  B54,
  input  B55,
  input  B56,
  input  B57,
  input  B58,
  input  B59,
  input  B60,
  input  B61,
  input  B62,
  input  B63,
  input  B64,
  input  C6,
  input  [1:0] in_195,
  output A1_2,
  output A2_2,
  output A3_2,
  output A4_2,
  output A5_2,
  output A6_2,
  output A7_2,
  output A8_2,
  output A9_2,
  output A10_2,
  output A11_2,
  output A12_2,
  output A13_2,
  output A14_2,
  output A15_2,
  output A16_2,
  output A17_2,
  output A18_2,
  output A19_2,
  output A20_2,
  output A21_2,
  output A22_2,
  output A23_2,
  output A24_2,
  output A25_2,
  output A26_2,
  output A27_2,
  output A28_2,
  output A29_2,
  output A30_2,
  output A31_2,
  output A32_2,
  output A33_2,
  output A34_2,
  output A35_2,
  output A36_2,
  output A37_2,
  output A38_2,
  output A39_2,
  output A40_2,
  output A41_2,
  output A42_2,
  output A43_2,
  output A44_2,
  output A45_2,
  output A46_2,
  output A47_2,
  output A48_2,
  output A49_2,
  output A50_2,
  output A51_2,
  output A52_2,
  output A53_2,
  output A54_2,
  output A55_2,
  output A56_2,
  output A57_2,
  output A58_2,
  output A59_2,
  output A60_2,
  output A61_2,
  output A62_2,
  output A63_2,
  output A64_2,
  output A65
);

  wire adder32bit_1_d1;

  ADDER32BIT adder32bit_1 (
    .A1(A33), .A2(A34), .A3(A35), .A4(A36), .A5(A37), .A6(A38), .A7(A39), .A8(A40), .A9(A41), .A10(A42),
    .A11(A43), .A12(A44), .A13(A45), .A14(A46), .A15(A47), .A16(A48), .A17(A49), .A18(A50), .A19(A51),
    .A20(A52), .A21(A53), .A22(A54), .A23(A55), .A24(A56), .A25(A57), .A26(A58), .A27(A59), .A28(A60),
    .A29(A61), .A30(A62), .A31(A63), .A32(A64), .B1(B33), .B2(B34), .B3(B35), .B4(B36), .B5(B37), .B6(B38),
    .B7(B39), .B8(B40), .B9(B41), .B10(B42), .B11(B43), .B12(B44), .B13(B45), .B14(B46), .B15(B47),
    .B16(B48), .B17(B49), .B18(B50), .B19(B51), .B20(B52), .B21(B53), .B22(B54), .B23(B55), .B24(B56),
    .B25(B57), .B26(B58), .B27(B59), .B28(B60), .B29(B61), .B30(B62), .B31(B63), .B32(B64), .C5(C6),
    .D1(adder32bit_1_d1), .D2(A34_2), .D3(A35_2), .D4(A36_2), .D5(A37_2), .D6(A38_2), .D7(A39_2), .D8(A40_2),
    .D9(A41_2), .D10(A42_2), .D11(A43_2), .D12(A44_2), .D13(A45_2), .D14(A46_2), .D15(A47_2), .D16(A48_2),
    .D17(A49_2), .D18(A50_2), .D19(A51_2), .D20(A52_2), .D21(A53_2), .D22(A54_2), .D23(A55_2), .D24(A56_2),
    .D25(A57_2), .D26(A58_2), .D27(A59_2), .D28(A60_2), .D29(A61_2), .D30(A62_2), .D31(A63_2), .D32(A64_2),
    .D33(A65));
  ADDER32BIT adder32bit_2 (
    .A1(A1), .A2(A2), .A3(A3), .A4(A4), .A5(A5), .A6(A6), .A7(A7), .A8(A8), .A9(A9), .A10(A10), .A11(A11),
    .A12(A12), .A13(A13), .A14(A14), .A15(A15), .A16(A16), .A17(A17), .A18(A18), .A19(A19), .A20(A20),
    .A21(A21), .A22(A22), .A23(A23), .A24(A24), .A25(A25), .A26(A26), .A27(A27), .A28(A28), .A29(A29),
    .A30(A30), .A31(A31), .A32(A32), .B1(B1), .B2(B2), .B3(B3), .B4(B4), .B5(B5), .B6(B6), .B7(B7), .B8(B8),
    .B9(B9), .B10(B10), .B11(B11), .B12(B12), .B13(B13), .B14(B14), .B15(B15), .B16(B16), .B17(B17),
    .B18(B18), .B19(B19), .B20(B20), .B21(B21), .B22(B22), .B23(B23), .B24(B24), .B25(B25), .B26(B26),
    .B27(B27), .B28(B28), .B29(B29), .B30(B30), .B31(B31), .B32(B32), .C5(adder32bit_1_d1), .D1(A1_2),
    .D2(A2_2), .D3(A3_2), .D4(A4_2), .D5(A5_2), .D6(A6_2), .D7(A7_2), .D8(A8_2), .D9(A9_2), .D10(A10_2),
    .D11(A11_2), .D12(A12_2), .D13(A13_2), .D14(A14_2), .D15(A15_2), .D16(A16_2), .D17(A17_2), .D18(A18_2),
    .D19(A19_2), .D20(A20_2), .D21(A21_2), .D22(A22_2), .D23(A23_2), .D24(A24_2), .D25(A25_2), .D26(A26_2),
    .D27(A27_2), .D28(A28_2), .D29(A29_2), .D30(A30_2), .D31(A31_2), .D32(A32_2), .D33(A33_2));
endmodule
