// Digital circuit ADDER8BIT.dig as structural Verilog
module ADDER8BIT (
  input  A1,
  input  A2,
  input  A3,
  input  A4,
  input  A5,
  input  A6,
  input  A7,
  input  A8,
  input  B1,
  input  B2,
  input  B3,
  input  B4,
  input  B5,
  input  B6,
  input  B7,
  input  B8,
  input  C3,
  output A,
  output B,
  output C,
  output D,
  output E,
  output F,
  output G,
  output H,
  output I
);

  wire adder4bit_1_a;

  ADDER4bit adder4bit_1 (
    .A1(A5), .A2(A6), .A3(A7), .A4(A8), .B1(B5), .B2(B6), .B3(B7), .B4(B8), .C2(C3), .A(adder4bit_1_a),
    .B(F), .C(G), .D(H), .E(I));
  ADDER4bit adder4bit_2 (
    .A1(A1), .A2(A2), .A3(A3), .A4(A4), .B1(B1), .B2(B2), .B3(B3), .B4(B4), .C2(adder4bit_1_a), .A(A), .B(B),
    .C(C), .D(D), .E(E));
endmodule
