// Digital circuit ANDGate.dig as structural Verilog
module ANDGate (
  input  B,
  input  A,
  output OUTPUT_AND
);

  wire A_s, B_s;

  NFET u_A (.G(A), .D(1'b1), .S(A_s));
  NFET u_B (.G(B), .D(A_s), .S(B_s));
  DiodeForward diodeforward_1 (.in(B_s), .out(OUTPUT_AND));
  PullDown pulldown_1 (.out(OUTPUT_AND));
endmodule
