// Digital circuit HALFADDER.dig as structural Verilog
module HALFADDER (
  input  A,
  input  B,
  output OUTPUT_A,
  output OUTPUT_B
);

  XORGate xorgate_1 (.A(A), .B(B), .OUTPUT(OUTPUT_B));
  ANDGate andgate_1 (.B(B), .A(A), .OUTPUT(OUTPUT_A));
endmodule
