// Digital circuit NANDGate.dig as structural Verilog
module NANDGate (
  input  B,
  input  A,
  output OUTPUT_NAND
);

  wire A_d;

  PFET u_A (.G(A), .S(1'b1), .D(A_d));
  PFET u_B (.G(B), .S(1'b1), .D(A_d));
  DiodeForward diodeforward_1 (.in(A_d), .out(OUTPUT_NAND));
  PullDown pulldown_1 (.out(OUTPUT_NAND));
endmodule
