// Digital circuit NORGate.dig as structural Verilog
module NORGate (
  input  A,
  input  B,
  output OUTPUT_NOR
);

  wire A_d, B_d;

  PFET u_A (.G(A), .S(1'b1), .D(A_d));
  PFET u_B (.G(B), .S(A_d), .D(B_d));
  DiodeForward diodeforward_1 (.in(B_d), .out(OUTPUT_NOR));
  PullDown pulldown_1 (.out(OUTPUT_NOR));
endmodule
