// Digital circuit NOTGate.dig as structural Verilog
module NOTGate (
  input  A,
  output OUTPUT_NOT
);

  wire A_s;

  PFET u_A (.G(A), .S(A_s), .D(1'b1));
  PullDown pulldown_1 (.out(OUTPUT_NOT));
  DiodeForward diodeforward_1 (.in(A_s), .out(OUTPUT_NOT));
endmodule
