// Digital circuit ORGate.dig as structural Verilog
module ORGate (
  input  A,
  input  B,
  output OUTPUT_OR
);

  wire A_s;

  NFET u_A (.G(A), .D(1'b1), .S(A_s));
  NFET u_B (.G(B), .D(1'b1), .S(A_s));
  DiodeForward diodeforward_1 (.in(A_s), .out(OUTPUT_OR));
  PullDown pulldown_1 (.out(OUTPUT_OR));
endmodule
