// Digital circuit TEST4BITADDER.dig as structural Verilog
module TEST4BITADDER (
  input  c8,
  input  sdas,
  input  adas,
  input  avadvdas,
  input  wwegwe,
  input  vasvasv,
  input  wrERV,
  input  QWQQW,
  input  FBFBR,
  input  QQQQ,
  input  c27,
  input  B27,
  input  B1,
  input  B2,
  input  B3,
  input  B4,
  input  B5,
  input  B6,
  input  B7,
  input  B8,
  input  A1,
  input  A2,
  input  A3,
  input  A4,
  input  A5,
  input  A6,
  input  A7,
  input  A8,
  input  C1,
  input  C2,
  input  C3,
  input  C4,
  input  D1,
  input  D2,
  input  D3,
  input  D4,
  input  E1,
  input  E2,
  input  F1,
  input  F2,
  input  carry,
  output A26,
  output A27,
  output A28,
  output A29,
  output A30,
  output A31,
  output A32,
  output F,
  output E,
  output D,
  output C,
  output out_53,
  output out_54,
  output out_55
);

  wire adder1bit_1_carry_a, adder1bit_2_carry_a, adder2bit_1_carry_a, adder2bit_1_output_c,
       adder2bit_2_carry_a, adder4bit_1_a, adder4bit_2_a, adder4bit_2_b, adder4bit_2_c, adder4bit_2_d,
       adder4bit_2_e, adder4bit_3_a, adder4bit_3_b, adder4bit_3_c, adder4bit_3_d, adder4bit_3_e;

  ADDER4bit adder4bit_1 (
    .A1(sdas), .A2(adas), .A3(avadvdas), .A4(wwegwe), .B1(wrERV), .B2(QWQQW), .B3(FBFBR), .B4(QQQQ),
    .A(adder4bit_1_a), .B(A29), .C(A30), .D(A31), .E(A32));
  ADDER1bit adder1bit_1 (.INPUT_CARRY_A(E2), .B(F2), .C(carry), .OUTPUT_B(out_55), .CARRY_A(adder1bit_1_carry_a));
  ADDER1bit adder1bit_2 (
    .INPUT_CARRY_A(adder4bit_1_a), .B(c8), .C(vasvasv), .OUTPUT_B(A28), .CARRY_A(adder1bit_2_carry_a));
  ADDER1bit adder1bit_3 (.INPUT_CARRY_A(E1), .B(F1), .C(adder1bit_1_carry_a), .OUTPUT_B(out_54), .CARRY_A(out_53));
  ADDER4bit adder4bit_2 (
    .A1(A1), .A2(A2), .A3(A3), .A4(A4), .B1(B1), .B2(B2), .B3(B3), .B4(B4), .A(adder4bit_2_a),
    .B(adder4bit_2_b), .C(adder4bit_2_c), .D(adder4bit_2_d), .E(adder4bit_2_e));
  ADDER4bit adder4bit_3 (
    .A1(A5), .A2(A6), .A3(A7), .A4(A8), .B1(B5), .B2(B6), .B3(B7), .B4(B8), .A(adder4bit_3_a),
    .B(adder4bit_3_b), .C(adder4bit_3_c), .D(adder4bit_3_d), .E(adder4bit_3_e));
  ADDER1bit adder1bit_4 (.INPUT_CARRY_A(adder1bit_2_carry_a), .B(c27), .C(B27), .OUTPUT_B(A27), .CARRY_A(A26));
  ADDER2bit adder2bit_1 (
    .A1(C1), .A2(C2), .B1(D1), .B2(D2), .OUTPUT_C(adder2bit_1_output_c), .OUTPUT_B(C),
    .CARRY_A(adder2bit_1_carry_a));
  ADDER2bit adder2bit_2 (.A1(C3), .A2(C4), .B1(D3), .B2(D4), .OUTPUT_C(F), .OUTPUT_B(E), .CARRY_A(adder2bit_2_carry_a));
  XORGate xorgate_1 (.A(adder2bit_2_carry_a), .B(adder2bit_1_output_c), .OUTPUT(D));
  ANDGate andgate_1 (.B(adder2bit_1_output_c), .A(adder2bit_2_carry_a), .OUTPUT_AND(C));
endmodule
