// Digital circuit XNORGate.dig as structural Verilog
module XNORGate (
  input  A,
  input  B,
  output OUTPUT_XNOR
);

  wire A_d, B_d;

  PFET u_A (.G(A), .S(1'b1), .D(A_d));
  PFET u_B (.G(B), .S(A_d), .D(B_d));
  NFET A_2 (.G(A), .D(B), .S(B_d));
  DiodeForward diodeforward_1 (.in(B_d), .out(OUTPUT_XNOR));
  PullDown pulldown_1 (.out(OUTPUT_XNOR));
endmodule
