// Digital circuit XORGate.dig as structural Verilog
module XORGate (
  input  A,
  input  B,
  output OUTPUT_XOR
);

  wire A_d, B_d;

  PFET u_A (.G(A), .S(1'b1), .D(A_d));
  NFET u_B (.G(B), .D(B_d), .S(A_d));
  PFET B_2 (.G(B), .S(A), .D(B_d));
  DiodeForward diodeforward_1 (.in(B_d), .out(OUTPUT_XOR));
  PullDown pulldown_1 (.out(OUTPUT_XOR));
endmodule
